# Fritzing sketch piWorkshop (saved by Fritzing 0.9.3b)
breadboards: 1

parts:
  Raspberry_Pi2 = Raspberry Pi B rev2
  LED1 = smd LED [color="Red (633nm)" package="1206 [SMD]"]
  LED2 = smd LED [color="Blue (525nm)" package="1206 [SMD]"]
  S1 = Momentary Switch [package=ksa_sealed_tac_switch]
  R1 = Resistor [tolerance=±5% resistance=330 package=THT]
  R2 = Resistor [tolerance=±5% resistance=330 package=THT]
  R3 = Resistor [tolerance=±5% resistance=1k package=THT]

nets:
  N1: Raspberry_Pi2.3V3, S1.2
  N2: Raspberry_Pi2.GND, R1.Pin_1, R2.Pin_1
  N3: Raspberry_Pi2.GPIO_23, LED2.anode
  N4: Raspberry_Pi2.GPIO_18, R3.Pin_0
  N5: Raspberry_Pi2.GPIO_24, LED1.anode
  N6: LED1.cathode, R1.Pin_0
  N7: LED2.cathode, R2.Pin_0
  N8: S1.4, R3.Pin_1
